// Logisim project Ctl_Data_Processing.circ as structural Verilog: 1 circuit, main circuit Data_Processing
module Data_Processing (
  input  Enable,
  input  [15:0] Instruction,
  output [2:0] Rd,
  output [2:0] Rn,
  output [2:0] Rm,
  output [3:0] ALU_Opcode,
  output [3:0] Flags_Update_Mask
);

  Multiplexer #(.enable("false"), .width(4)) multiplexer_1 (
    .in0(4'b0000), .in1(Instruction[9:6]), .out(ALU_Opcode), .sel(Enable));

  // Other names for the same wires on the sheet: b6 = Instruction[6]; b7 = Instruction[7]; b8 = Instruction[8];
  //   b9 = Instruction[9]; en = Enable; b0 = Instruction[0]; b1 = Instruction[1]; b2 = Instruction[2];
  //   b3 = Instruction[3]; b4 = Instruction[4]; b5 = Instruction[5]; b10 = Instruction[10]; b11 = Instruction[11];
  //   b12 = Instruction[12]; b13 = Instruction[13]; b14 = Instruction[14]; b15 = Instruction[15]

  // Notes on the sheet:
  //   Pull output low on Enable = 0
  //   Note 2: RSB instruction has Rn as 1st operand.
  //   MUL instruction has Rn as 1st operand and Rdm as 2nd operand
  //   For simplification purposes, Rm is used for 1st operand both here and in the ALU.
  //   Note: instructions that does not save the result will still have the second operand as the destination register, the ALU will copy the second register to the destination register
endmodule
